# Fritzing sketch rasp-nRF24 (saved by Fritzing 0.9.2b)

parts:
  Raspberry_Pi1 = Raspberry Pi B rev2
  NRF24L4 = NRF24L01

nets:
  3V3: Raspberry_Pi1.3V3, NRF24L4.VCC
  GND: Raspberry_Pi1.GND, NRF24L4.GND
  N1: Raspberry_Pi1.GPIO_24, NRF24L4.CE
  N2: Raspberry_Pi1.GPIO_10, NRF24L4.MOSI
  N3: Raspberry_Pi1.GPIO_9, NRF24L4.MISO
  N4: Raspberry_Pi1.GPIO_11, NRF24L4.SCK
  N5: Raspberry_Pi1.GPIO_8, NRF24L4.CSN

notes:
  pin utilisé:
  CE: GPIO24
  CSN: GPIO8

custom parts:
  NRF24L01: NRF24L01 module
